// Logisim project ALU.circ as structural Verilog: 13 circuits, main circuit Adder_1
// ALU
module main (
  input  Ctrl,
  input  [7:0] A,
  input  [7:0] B,
  input  [4:0] Selectors,
  input  OE,
  output [7:0] ALU_Dout,
  output [7:0] ALU_Result,
  output Cout
);

  ALU alu_1 (.Control(Selectors), .A(A), .B(B), .Enable(Ctrl), .C(Cout), .OUTPUT(ALU_Result));  // open: N, V, Z
  assign ALU_Dout = OE ? ALU_Result : 8'bz;  // Controlled_Buffer controlled_buffer_1
endmodule

module Adder_1 (
  input  [7:0] A,
  input  [7:0] B,
  output [7:0] OUTPUT,
  output C
);

  Adder adder_1 (.a(A), .b(B), .out(OUTPUT), .cout(C));  // open: cin
endmodule

module Sub (
  input  [7:0] A,
  input  [7:0] B,
  output [7:0] OUTPUT,
  output N
);

  Subtractor subtractor_1 (.a(A), .b(B), .out(OUTPUT), .bout(N));  // open: bin
endmodule

module LogicUnit (
  input  [7:0] A,
  input  [7:0] B,
  output [7:0] AndOut,
  output [7:0] OrOut,
  output [7:0] NotOut,
  output [7:0] XorOut
);

  assign AndOut = A & B;  // AND_Gate and_1, 8 bits wide
  assign OrOut = A | B;  // OR_Gate or_1, 8 bits wide
  assign NotOut = ~A;  // NOT_Gate not_1, 8 bits wide
  assign XorOut = A ^ B;  // XOR_Gate xor_1, 8 bits wide
endmodule

module Inc (
  input  [7:0] A,
  output [7:0] OUTPUT,
  output C
);

  Adder adder_1 (.a(A), .b(8'h1), .out(OUTPUT), .cout(C));  // open: cin
endmodule

module Dec (
  input  [7:0] A,
  output [7:0] OUTPUT,
  output N
);

  Subtractor subtractor_1 (.a(A), .b(8'h1), .out(OUTPUT), .bout(N));  // open: bin
endmodule

module Comp (
  input  [7:0] A,
  input  [7:0] B,
  output [7:0] out_3
);

  wire comparator_1_lt;

  Comparator comparator_1 (.a(A), .b(B), .lt(comparator_1_lt));  // open: gt, eq
  assign out_3 = {{7{comparator_1_lt}}, comparator_1_lt};  // Bit_Extender bit_extender_1
endmodule

module Shifter_1 (
  input  [7:0] A,
  input  [2:0] Distance,
  output [7:0] Logical_Left,
  output [7:0] Logical_Right,
  output [7:0] Arithmetic_Right_bb1b6ef0
);

  Shifter shifter_1 (.in(A), .\dist (Distance), .out(Logical_Left));
  Shifter #(.shift("lr")) shifter_2 (.in(A), .\dist (Distance), .out(Logical_Right));
  Shifter #(.shift("ar")) shifter_3 (.in(A), .\dist (Distance), .out(Arithmetic_Right_bb1b6ef0));
endmodule

module ALU (
  input  [7:0] A,
  input  [7:0] B,
  input  Enable,
  input  [4:0] Control,
  output [7:0] OUTPUT,
  output C,
  output V,
  output N,
  output Z
);

  wire adder_1_1_c, dec_1_n, inc_1_c, sub_1_n;
  wire [7:0] adder_1_1_output, comp_1_out_3, compunsigned_1_out_3, dec_1_output, inc_1_output, Logic_andout,
       Logic_notout, Logic_orout, Logic_xorout, shifter_1_1_arithmetic_right_bb1b6ef0,
       shifter_1_1_logical_left, shifter_1_1_logical_right, sub_1_output;

  carry_logic carry_logic_1 (.adder_carry(adder_1_1_c), .Control(Control), .inc_carry(inc_1_c), .OUTPUT(C));
  negative_logic negative_logic_1 (.sub_negative(sub_1_n), .Control(Control), .dec_negative(dec_1_n), .OUTPUT(N));
  Adder_1 adder_1_1 (.A(A), .B(B), .OUTPUT(adder_1_1_output), .C(adder_1_1_c));
  Sub sub_1 (.A(A), .B(B), .OUTPUT(sub_1_output), .N(sub_1_n));
  LogicUnit Logic (
    .A(A), .B(B), .AndOut(Logic_andout), .OrOut(Logic_orout), .NotOut(Logic_notout), .XorOut(Logic_xorout));
  Inc inc_1 (.A(A), .OUTPUT(inc_1_output), .C(inc_1_c));
  Dec dec_1 (.A(A), .OUTPUT(dec_1_output), .N(dec_1_n));
  Comp comp_1 (.A(A), .B(B), .out_3(comp_1_out_3));
  CompUnsigned compunsigned_1 (.A(A), .B(B), .out_3(compunsigned_1_out_3));
  Shifter_1 shifter_1_1 (
    .A(A), .Distance(B[2:0]), .Logical_Left(shifter_1_1_logical_left),
    .Logical_Right(shifter_1_1_logical_right),
    .Arithmetic_Right_bb1b6ef0(shifter_1_1_arithmetic_right_bb1b6ef0));
  Multiplexer #(.enable("true"), .select(5), .width(8)) multiplexer_1 (
    .in0(adder_1_1_output), .in1(sub_1_output), .in2(Logic_andout), .in3(Logic_orout), .in4(Logic_notout),
    .in5(Logic_xorout), .in6(inc_1_output), .in7(dec_1_output), .in8(comp_1_out_3),
    .in9(compunsigned_1_out_3), .in10(shifter_1_1_logical_left), .in11(shifter_1_1_logical_right),
    .in12(shifter_1_1_arithmetic_right_bb1b6ef0), .in13({8{1'b0}}), .in14({8{1'b0}}), .in15({8{1'b0}}),
    .in16({8{1'b0}}), .in17({8{1'b0}}), .in18({8{1'b0}}), .in19({8{1'b0}}), .in20({8{1'b0}}),
    .in21({8{1'b0}}), .in22({8{1'b0}}), .in23({8{1'b0}}), .in24({8{1'b0}}), .in25({8{1'b0}}),
    .in26({8{1'b0}}), .in27({8{1'b0}}), .in28({8{1'b0}}), .in29({8{1'b0}}), .in30({8{1'b0}}),
    .in31({8{1'b0}}), .out(OUTPUT), .sel(Control), .en(Enable));
  overflow_logic Overflow (.A(A), .B(B), .OUTPUT(OUTPUT), .Control(Control), .Overflow(V));
  Comparator comparator_1 (.a(OUTPUT), .b({8{1'b0}}), .eq(Z));  // open: gt, lt
endmodule

module carry_logic (
  input  adder_carry,
  input  [4:0] Control,
  input  inc_carry,
  output OUTPUT
);

  wire and_1_out, and_2_out, comparator_1_eq, comparator_2_eq;

  Comparator #(.width(5)) comparator_1 (.a(Control), .b({5{1'b0}}), .eq(comparator_1_eq));  // open: gt, lt
  Comparator #(.width(5)) comparator_2 (.a(Control), .b(5'b00110), .eq(comparator_2_eq));  // open: gt, lt
  and and_1 (and_1_out, comparator_1_eq, adder_carry);
  and and_2 (and_2_out, inc_carry, comparator_2_eq);
  or or_1 (OUTPUT, and_1_out, and_2_out);
endmodule

module CompUnsigned (
  input  [7:0] A,
  input  [7:0] B,
  output [7:0] out_3
);

  wire comparator_1_lt;

  Comparator #(.mode("unsigned")) comparator_1 (.a(A), .b(B), .lt(comparator_1_lt));  // open: gt, eq
  assign out_3 = {{7{comparator_1_lt}}, comparator_1_lt};  // Bit_Extender bit_extender_1
endmodule

module negative_logic (
  input  sub_negative,
  input  [4:0] Control,
  input  dec_negative,
  output OUTPUT
);

  wire and_1_out, and_2_out, comparator_1_eq, comparator_2_eq;

  Comparator #(.width(5)) comparator_1 (.a(Control), .b(5'b00001), .eq(comparator_1_eq));  // open: gt, lt
  Comparator #(.width(5)) comparator_2 (.a(Control), .b(5'b00111), .eq(comparator_2_eq));  // open: gt, lt
  and and_1 (and_1_out, comparator_1_eq, sub_negative);
  and and_2 (and_2_out, dec_negative, comparator_2_eq);
  or or_1 (OUTPUT, and_1_out, and_2_out);
endmodule

module overflow_logic (
  input  [7:0] A,
  input  [7:0] B,
  input  [7:0] OUTPUT,
  input  [4:0] Control,
  output Overflow
);

  wire comparator_1_eq, comparator_2_eq, comparator_3_eq, comparator_4_eq, comparator_5_eq, comparator_6_eq,
       not_1_out, or_1_out;

  Comparator #(.mode("unsigned"), .width(1)) comparator_1 (.a(A[7]), .b(B[7]), .eq(comparator_1_eq));  // open: gt, lt
  Comparator #(.mode("unsigned"), .width(1)) comparator_2 (
    .a(A[7]), .b(OUTPUT[7]), .eq(comparator_2_eq));  // open: gt, lt
  Comparator #(.mode("unsigned"), .width(5)) comparator_3 (
    .a(Control), .b({5{1'b0}}), .eq(comparator_3_eq));  // open: gt, lt
  Comparator #(.mode("unsigned"), .width(5)) comparator_4 (
    .a(Control), .b(5'b00001), .eq(comparator_4_eq));  // open: gt, lt
  Comparator #(.mode("unsigned"), .width(5)) comparator_5 (
    .a(Control), .b(5'b00110), .eq(comparator_5_eq));  // open: gt, lt
  Comparator #(.mode("unsigned"), .width(5)) comparator_6 (
    .a(Control), .b(5'b00111), .eq(comparator_6_eq));  // open: gt, lt
  not not_1 (not_1_out, comparator_2_eq);
  or or_1 (or_1_out, comparator_3_eq, comparator_4_eq, comparator_5_eq, comparator_6_eq);
  and and_1 (Overflow, comparator_1_eq, or_1_out, not_1_out);

  // Notes on the sheet:
  //   Make sure that overflow is only possible when adding, subtracting, incrementing or decrementing
endmodule
